// Digital circuit IR.dig as structural Verilog
module IR (
  input  [7:0] Input_IR,
  input  CLK,
  input  [7:0] CTRL_LD,
  input  [7:0] SRAM_Data,
  output [7:0] Output_IR
);

  wire [7:0] multiplexer_1_out;

  Multiplexer #(.Bits(8)) multiplexer_1 (.sel(CTRL_LD[1]), .in_0(SRAM_Data), .in_1(Input_IR), .out(multiplexer_1_out));
  Register #(.Bits(8)) IR_REG (.D(multiplexer_1_out), .C(CLK), .en(CTRL_LD[0]), .Q(Output_IR));

  // Notes on the sheet:
  //   CTRL_LD: LD
endmodule
